# Fritzing sketch breadboard (saved by Fritzing 0.9.3b)
breadboards: 1

parts:
  Adafruit_HUZZAH_ESP8266_Breakout1 = Adafruit HUZZAH ESP8266 Breakout [part_number=2471]
  74LVC245_Level_Shifter = IC, DIP package, 20 pins [chip_label=74LVC245 part_number=74LVC245]
  74LVC245_Level_Shifter1 = IC, DIP package, 20 pins [chip_label=74LVC245 part_number=74LVC245]
  roomba_mini_din = DIN7 [part_number="roomba mini din connector" package=din7]

nets:
  N1: Adafruit_HUZZAH_ESP8266_Breakout1.GND, 74LVC245_Level_Shifter.pin10, 74LVC245_Level_Shifter.pin19, 74LVC245_Level_Shifter1.pin10, 74LVC245_Level_Shifter1.pin19, roomba_mini_din.7
  N2: Adafruit_HUZZAH_ESP8266_Breakout1.#5, 74LVC245_Level_Shifter.pin4
  N3: Adafruit_HUZZAH_ESP8266_Breakout1.#2, 74LVC245_Level_Shifter.pin3
  N4: 74LVC245_Level_Shifter.pin1, 74LVC245_Level_Shifter.pin20
  N5: 74LVC245_Level_Shifter.pin16, roomba_mini_din.5
  N6: 74LVC245_Level_Shifter.pin17, roomba_mini_din.3
  N7: 74LVC245_Level_Shifter1.pin1, 74LVC245_Level_Shifter1.pin20

notes:
  <-- 3.3v rail
  <-- 5v rail
